# Fritzing sketch esp8266 (saved by Fritzing 0.9.3b)
circuit board: 6.78598cm x 3.38742cm
perfboards: 1

parts:
  U1 = 74AHCT125 [part_number=SN74AHCT125 package=dil14]
  C1 = Electrolytic Capacitor [capacitance=10µF package="100 mil [THT, electrolytic]"]
  R1 = Resistor [tolerance=±5% resistance=330 package=THT]
  U2 = Voltage Regulator [package=to220-adj]
  JP1 = Header 6 [package=molex-1x6_lock]
  Gizwits_WiFi_Witty_ESP-12F1 = Gizwits WiFi Witty ESP-12F
  C2 = Electrolytic Capacitor [capacitance=10µF package="100 mil [THT, electrolytic]"]

nets:
  GND: U1.GND, U1.4OE, C1.-, U2.GND, JP1.2, Gizwits_WiFi_Witty_ESP-12F1.GND, C2.-
  N1: U1.4Y, R1.Pin_1
  N2: U1.4A, Gizwits_WiFi_Witty_ESP-12F1.D5
  VCC: U1.VCC, U2.Vin, JP1.1, C2.+
  N3: C1.+, U2.Vout, Gizwits_WiFi_Witty_ESP-12F1.VCC
  N4: R1.Pin_0, JP1.3

custom parts:
  74AHCT125: Quad Level-Shifter (3V to 5V) Quadruple Bus Buffer Gates With 3-State Outputs
  Voltage Regulator: Voltage Regulator Standard LM317 adjustable voltage regulator. AOI (Adjust Output Input). Google 'LM317 Calculator' for easy to use app to get the two resistor values needed. 240/720 for 5V output. 240/390 for 3.3V output. Spark Fun Electronics SKU : COM-00527
  Gizwits WiFi Witty ESP-12F: A breadboard friendly two part WiFi development board by Gizwits, powered by an ESP8266 ESP-12F SoC, featuring twin micro-usb ports, a photoresistor, a WS2812 RGB-LED and three buttons. The board comes in two parts. The bottom half has reset and flash buttons, a micro-usb with CH340 UART and 2x 1x08 female headers. The top half has the ESP-12F, LDR, RGB-LED, micro-usb (for power only), an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
